// Digital circuit MiniCPU.dig as structural Verilog
module MiniCPU (
  input  [7:0] M,
  input  [7:0] N,
  input  [13:0] progIn,
  input  reset,
  input  progLoad,
  input  start,
  input  result,
  input  clk,
  output valid,
  output done,
  output [7:0] \output ,
  output [13:0] checkInput,
  output [7:0] out_13,
  output [7:0] out_14,
  output [7:0] out_15,
  output [7:0] out_16,
  output [5:0] out_17,
  output [7:0] out_18,
  output [5:0] out_19,
  output [7:0] out_20,
  output [7:0] out_21,
  output [7:0] out_22,
  output [7:0] out_23,
  output [7:0] out_24,
  output [7:0] out_25,
  output [7:0] out_26,
  output [7:0] out_27,
  output [7:0] out_28,
  output [7:0] out_29,
  output [15:0] out_30
);

  wire A_Fact__eq__0, accA___accA___accB, accA___accA___accB_t, accA___accA___accB_t_t,
       accA___accA___accB_t_t_t, accA___accA___accB_t_t_t_t, accA___accA__gt__gt__accB,
       accA___accA__gt__gt__gt__accB, accA___accA__lt__lt__accB, accA___accA__lt__lt__lt__accB,
       accA___accA__plus__accB, accA___accA_AND_accB, accA___accA_OR_accB, accA___accA_XOR_accB,
       accA___NOT_accA, accA___pRAM_adr_Operand, accA___regC___accB___regD, accA___rRAM_adr_Operand,
       accA__lt__accB, accA__lt__Operand, accA__lt__regC, accA__lt__regD, accA_CMP_accB, accB___accA,
       accB__lt__accA, accB__lt__Operand, and_4_out, and_5_out, and_6_out, and_7_out, and_8_out, BUSY,
       busy_Fact, busy_lcm, comparator_2_eq, comparator_2_gt, Compare_2_eq, Compare_eq, d_ff_8_q, eneq, eq,
       equal, Future_1, Future_2, greater, gt, holdresult, holdstart, holdstop, isPrime_accA, jump,
       Jump_to_address_Operand, Jump_to_address_Operand_if_eq, Jump_to_address_Operand_if_eq_or_gr,
       Jump_to_address_Operand_if_eq_or_le, Jump_to_address_Operand_if_gr, Jump_to_address_Operand_if_le,
       lesser, lt, multiplexer_1_out, multiplexer_2_out, multiplexer_3_out, multiplexer_4_out,
       multiplexer_5_out, Nope, not_1_out, not_2_out, not_3_out, notconnected_1_out, notconnected_2_out,
       notconnected_3_out, notconnected_4_out, notconnected_5_out, notconnected_6_out, notconnected_7_out,
       notconnected_8_out, notconnected_9_out, notconnected_10_out, notconnected_11_out, notconnected_14_out,
       or_1_out, or_3_out, or_4_out, or_5_out, or_6_out, or_8_out, or_9_out, or_10_out, or_12_out, or_13_out,
       or_18_out, or_19_out, or_20_out, or_25_out, or_27_out, or_28_out, prime_d, Q1_Fact, Q1_lcm, Q2_Fact,
       Q2_lcm, Q3_Fact, regC___M___regD___N, regC__lt__accA, regC__lt__M, regC__lt__N, regD__lt__accA,
       regD__lt__M, regD__lt__N, resetovf, resultovf,
       rRAM_0x0E_0x0F____LCM__rRAM_adr_Operand__7_4______rRAM_adr_Operand__3_0, rRAM_adr_Operand____accA,
       S0_Fact, S0_lcm, S1_Fact, S1_lcm, S2_Fact, S2_lcm, S3_Fact, S4_Fact, SelA, SelB, SelC, SelD,
       setAB_Fact, STOP;
  wire [7:0] A___B, A__gt__gt__B, A__gt__gt__gt__B, A__lt__B, A__lt__C, A__lt__D, A__lt__lt__B,
       A__lt__lt__lt__B, A__lt__operand, A__lt__pRAM, A__lt__rRAM, A_and_B, A_B, A_B_2_mul, A_B___A_B_q,
       A_B_s, A_B_t, A_B_t_t, A_B_t_t_t, A_B_t_t_t_t, A_or_B, A_plus_B, A_plus_B_s, A_t, A_xor_B, add_1_s,
       Ainput, and_3_out, B__lt__A, B__lt__D, B__lt__operand, barrelshifter_1_out, barrelshifter_2_out,
       barrelshifter_3_out, barrelshifter_4_out, Binput, C__lt__A, C__lt__M, C__lt__N, counter_1_out,
       counter_2_out, counter_3_out, D__lt__A, D__lt__M, D__lt__N, d_ff_6_q, d_ff_7_q, input_C, input_D, M_t,
       multiplexer_8_out, multiplexer_9_out, multiplexer_10_out, multiplexer_11_out, multiplexer_12_out,
       multiplexer_13_out, multiplexer_14_out, multiplexer_15_out, multiplexer_16_out, multiplexer_17_out,
       multiplexer_18_out, multiplexer_19_out, multiplexer_22_out, multiplexer_30_out, multiplexer_32_out,
       multiplexer_37_out, multiplexer_38_out, multiplexer_42_out, multiplexer_60_out, N_t, not_4_out,
       notconnected_12_out, notconnected_13_out, or_26_out, rRAM__lt__A, xor_1_out;
  wire [13:0] pRAM_d2;
  wire [15:0] A_1_Fact, A_B_Fact, A_Fact, B_Fact, mul_2_mul, mul_3_mul, mul_4_mul, mul_5_mul, mul_6_mul,
       mul_7_mul, multiplexer_6_out, multiplexer_7_out;
  wire [31:16] mul_1_mul;

  or or_1 (or_1_out, reset, holdresult);
  RS_FF_AS rs_ff_as_1 (.S(STOP), .R(reset), .Q(valid));  // open: nQ
  RS_FF_AS rs_ff_as_2 (.S(resultovf), .R(or_1_out), .Q(done));  // open: nQ
  Seven_Seg_Hex seven_seg_hex_1 (.d(out_23[7:4]), .dp(1'b0));
  Seven_Seg_Hex seven_seg_hex_2 (.d(out_23[3:0]), .dp(1'b0));
  Multiplexer #(.Selector_Bits(2)) multiplexer_1 (
    .sel({Q1_lcm, Q2_lcm}), .in_0(1'b0), .in_1(1'b1), .in_2(1'b0), .in_3(notconnected_1_out),
    .out(multiplexer_1_out));
  // NotConnected on notconnected_1_out
  Multiplexer #(.Selector_Bits(3)) multiplexer_2 (
    .sel({Q1_Fact, Q2_Fact, Q3_Fact}), .in_0(1'b0), .in_1(1'b0), .in_2(1'b0), .in_3(1'b1), .in_4(1'b0),
    .in_5(notconnected_2_out), .in_6(notconnected_3_out), .in_7(notconnected_4_out), .out(multiplexer_2_out));
  // NotConnected on notconnected_2_out
  // NotConnected on notconnected_3_out
  // NotConnected on notconnected_4_out
  Decoder #(.Selector_Bits(3)) decoder_1 (
    .sel({Q1_Fact, Q2_Fact, Q3_Fact}), .out_0(S0_Fact), .out_1(S1_Fact), .out_2(S2_Fact), .out_3(S3_Fact),
    .out_4(S4_Fact));  // open: out_5, out_6, out_7
  or or_2 (setAB_Fact, S0_Fact, S2_Fact);
  RS_FF_AS rs_ff_as_3 (.S(STOP), .R(reset), .Q(holdstop));  // open: nQ
  Decoder #(.Selector_Bits(2)) decoder_2 (
    .sel({Q1_lcm, Q2_lcm}), .out_0(S0_lcm), .out_1(S1_lcm), .out_2(S2_lcm));  // open: out_3
  D_FF d_ff_1 (.D(multiplexer_2_out), .C(clk), .Q(Q1_Fact));  // open: nQ
  not not_1 (not_1_out, clk);
  or or_3 (or_3_out, reset, start);
  or or_4 (or_4_out, reset, start);
  D_FF d_ff_2 (.D(multiplexer_1_out), .C(clk), .Q(Q1_lcm));  // open: nQ
  Register #(.Bits(8)) register_1 (.D(N), .C(not_1_out), .en(or_3_out), .Q(N_t));
  Register #(.Bits(8)) register_2 (.D(M), .C(not_2_out), .en(or_4_out), .Q(M_t));
  not not_2 (not_2_out, clk);
  or or_5 (or_5_out, holdresult, STOP, reset);
  or or_6 (or_6_out, resultovf, reset);
  RS_FF_AS rs_ff_as_4 (.S(start), .R(or_5_out), .Q(holdstart));  // open: nQ
  RS_FF_AS rs_ff_as_5 (.S(result), .R(or_6_out), .Q(holdresult));  // open: nQ
  Multiplexer #(.Selector_Bits(2)) multiplexer_3 (
    .sel({Q1_lcm, Q2_lcm}), .in_0(rRAM_0x0E_0x0F____LCM__rRAM_adr_Operand__7_4______rRAM_adr_Operand__3_0),
    .in_1(1'b0), .in_2(1'b0), .in_3(notconnected_5_out), .out(multiplexer_3_out));
  // NotConnected on notconnected_5_out
  and and_1 (busy_lcm, ~S2_lcm, rRAM_0x0E_0x0F____LCM__rRAM_adr_Operand__7_4______rRAM_adr_Operand__3_0);  // And
  Multiplexer #(.Selector_Bits(3)) multiplexer_4 (
    .sel({Q1_Fact, Q2_Fact, Q3_Fact}), .in_0(1'b0), .in_1(1'b1), .in_2(1'b0), .in_3(1'b0), .in_4(1'b0),
    .in_5(notconnected_6_out), .in_6(notconnected_7_out), .in_7(notconnected_8_out), .out(multiplexer_4_out));
  // NotConnected on notconnected_6_out
  // NotConnected on notconnected_7_out
  // NotConnected on notconnected_8_out
  D_FF d_ff_3 (.D(multiplexer_3_out), .C(clk), .Q(Q2_lcm));  // open: nQ
  D_FF d_ff_4 (.D(multiplexer_4_out), .C(clk), .Q(Q2_Fact));  // open: nQ
  and and_2 (busy_Fact, ~S4_Fact, Future_1);  // And
  Multiplexer #(.Selector_Bits(3)) multiplexer_5 (
    .sel({Q1_Fact, Q2_Fact, Q3_Fact}), .in_0(Future_1), .in_1(A_Fact__eq__0), .in_2(1'b1), .in_3(1'b0),
    .in_4(1'b0), .in_5(notconnected_9_out), .in_6(notconnected_10_out), .in_7(notconnected_11_out),
    .out(multiplexer_5_out));
  // NotConnected on notconnected_9_out
  // NotConnected on notconnected_10_out
  // NotConnected on notconnected_11_out
  Sub #(.Bits(16)) sub_1 (.a(A_Fact), .b(16'h1), .c_i(1'b0), .s(A_1_Fact));  // open: c_o
  Multiplexer #(.Bits(16)) multiplexer_6 (
    .sel(S0_Fact), .in_0(A_1_Fact), .in_1({{13{1'b0}}, out_14[2:0]}), .out(multiplexer_6_out));
  Multiplexer #(.Bits(16)) multiplexer_7 (.sel(S0_Fact), .in_0(A_B_Fact), .in_1(16'h1), .out(multiplexer_7_out));
  Mul #(.Bits(16)) mul_1 (.a(A_Fact), .b(B_Fact), .mul({mul_1_mul, A_B_Fact}));
  Add #(.Bits(8)) add_1 (.a(d_ff_7_q), .b(8'h1), .c_i(1'b0), .s(add_1_s));  // open: c_o
  Comparator #(.Bits(16)) comparator_1 (.a(A_Fact), .b({16{1'b0}}), .eq(A_Fact__eq__0));  // open: gt, lt
  D_FF d_ff_5 (.D(multiplexer_5_out), .C(clk), .Q(Q3_Fact));  // open: nQ
  Register #(.Bits(16)) u_A_Fact (.D(multiplexer_6_out), .C(clk), .en(setAB_Fact), .Q(A_Fact));
  Register #(.Bits(16)) u_B_Fact (.D(multiplexer_7_out), .C(clk), .en(setAB_Fact), .Q(B_Fact));
  Multiplexer #(.Bits(8)) multiplexer_8 (.sel(BUSY), .in_0(add_1_s), .in_1(d_ff_7_q), .out(multiplexer_8_out));
  Multiplexer #(.Bits(8)) multiplexer_9 (
    .sel(accA___pRAM_adr_Operand), .in_0({8{1'b0}}), .in_1(out_18), .out(multiplexer_9_out));
  Multiplexer #(.Bits(8)) multiplexer_10 (
    .sel(holdstart), .in_0({8{1'b0}}), .in_1(multiplexer_8_out), .out(multiplexer_10_out));
  Multiplexer #(.Selector_Bits(2), .Bits(8)) multiplexer_11 (
    .sel({S4_Fact, S3_Fact}), .in_0(out_14), .in_1(B_Fact[15:8]), .in_2(B_Fact[7:0]),
    .in_3(notconnected_12_out), .out(multiplexer_11_out));
  // NotConnected on notconnected_12_out
  Multiplexer #(.Bits(8)) multiplexer_12 (.sel(S1_lcm), .in_0(8'hf), .in_1(8'he), .out(multiplexer_12_out));
  Multiplexer #(.Selector_Bits(2), .Bits(8)) multiplexer_13 (
    .sel({S4_Fact, S3_Fact}), .in_0({4'b0000, out_18[7:4]}), .in_1(8'ha), .in_2(8'hb),
    .in_3(notconnected_13_out), .out(multiplexer_13_out));
  // NotConnected on notconnected_13_out
  or or_7 (BUSY, busy_lcm, busy_Fact);
  Counter #(.Bits(8)) counter_1 (.en(progLoad), .C(clk), .clr(reset), .out(counter_1_out));  // open: ovf
  Multiplexer #(.Bits(8)) multiplexer_14 (
    .sel(jump), .in_0(multiplexer_10_out), .in_1(out_18), .out(multiplexer_14_out));
  Multiplexer #(.Bits(8)) multiplexer_15 (
    .sel(S0_lcm), .in_0(multiplexer_12_out), .in_1(multiplexer_13_out), .out(multiplexer_15_out));
  D_FF #(.Bits(8)) d_ff_6 (.D(multiplexer_14_out), .C(clk), .Q(d_ff_6_q));  // open: nQ
  not not_3 (not_3_out, clk);
  D_FF #(.Bits(8)) d_ff_7 (.D(d_ff_6_q), .C(not_3_out), .Q(d_ff_7_q));  // open: nQ
  Multiplexer #(.Bits(8)) multiplexer_16 (
    .sel(rRAM_adr_Operand____accA), .in_0(multiplexer_15_out), .in_1(out_18), .out(multiplexer_16_out));
  Multiplexer #(.Bits(8)) multiplexer_17 (.sel(S1_lcm), .in_0(out_24), .in_1(out_25), .out(multiplexer_17_out));
  D_FF d_ff_8 (.D(holdresult), .C(clk), .Q(d_ff_8_q));  // open: nQ
  Multiplexer #(.Bits(8)) multiplexer_18 (
    .sel(progLoad), .in_0(multiplexer_9_out), .in_1(counter_1_out), .out(multiplexer_18_out));
  or or_8 (or_8_out, ~S0_lcm, S3_Fact, S4_Fact, rRAM_adr_Operand____accA, reset);  // Or
  Counter #(.Bits(8)) counter_2 (.en(clk), .C(clk), .clr(resetovf), .out(counter_2_out), .ovf(resetovf));
  Multiplexer #(.Bits(8)) multiplexer_19 (
    .sel(S0_lcm), .in_0(multiplexer_17_out), .in_1(multiplexer_11_out), .out(multiplexer_19_out));
  Multiplexer #(.Bits(8)) multiplexer_20 (.sel(reset), .in_0(multiplexer_16_out), .in_1(counter_2_out), .out(out_28));
  Multiplexer #(.Bits(8)) multiplexer_21 (.sel(reset), .in_0(multiplexer_19_out), .in_1({8{1'b0}}), .out(out_29));
  Multiplexer #(.Bits(8)) multiplexer_22 (
    .sel(accA___rRAM_adr_Operand), .in_0({4'b0000, out_18[3:0]}), .in_1(out_18), .out(multiplexer_22_out));
  Counter #(.Bits(8)) counter_3 (.en(d_ff_8_q), .C(clk), .clr(resultovf), .out(counter_3_out));  // open: ovf
  or or_9 (or_9_out, holdresult, rRAM_0x0E_0x0F____LCM__rRAM_adr_Operand__7_4______rRAM_adr_Operand__3_0, accA___rRAM_adr_Operand);
  Multiplexer #(.Bits(8)) multiplexer_23 (
    .sel(accA__lt__Operand), .in_0({8{1'b0}}), .in_1(out_18), .out(A__lt__operand));
  Multiplexer #(.Bits(8)) multiplexer_24 (.sel(accA__lt__accB), .in_0({8{1'b0}}), .in_1(out_15), .out(A__lt__B));
  Multiplexer #(.Bits(8)) multiplexer_25 (.sel(or_12_out), .in_0({8{1'b0}}), .in_1(out_20), .out(A__lt__C));
  Multiplexer #(.Bits(8)) multiplexer_26 (.sel(accA__lt__regD), .in_0({8{1'b0}}), .in_1(out_14), .out(A__lt__D));
  Multiplexer #(.Bits(8)) multiplexer_27 (
    .sel(accA___pRAM_adr_Operand), .in_0({8{1'b0}}), .in_1(checkInput[7:0]), .out(A__lt__pRAM));
  Multiplexer #(.Bits(8)) multiplexer_28 (
    .sel(accA___rRAM_adr_Operand), .in_0({8{1'b0}}), .in_1(out_23), .out(A__lt__rRAM));
  Multiplexer #(.Bits(8)) multiplexer_29 (
    .sel(rRAM_adr_Operand____accA), .in_0({8{1'b0}}), .in_1(out_14), .out(rRAM__lt__A));
  Multiplexer #(.Bits(8)) multiplexer_30 (.sel(holdstop), .in_0(d_ff_6_q), .in_1({8{1'b0}}), .out(multiplexer_30_out));
  Multiplexer #(.Bits(8)) multiplexer_31 (
    .sel(holdresult), .in_0(multiplexer_22_out), .in_1(counter_3_out), .out(out_13));
  Comparator #(.Bits(8)) comparator_2 (
    .a(counter_3_out), .b(8'h10), .gt(comparator_2_gt), .eq(comparator_2_eq));  // open: lt
  Multiplexer #(.Bits(8)) multiplexer_32 (.sel(reset), .in_0(Ainput), .in_1({8{1'b0}}), .out(multiplexer_32_out));
  or or_10 (or_10_out, SelA, reset);
  RAMDualAccess #(.AddrBits(8), .Bits(8)) rRAM (
    .str(or_8_out), .C(clk), .ld(or_9_out), .A1(out_28), .Din1(out_29), .A2(out_13), .D1(out_22), .D2(out_23));
  or or_11 (resultovf, comparator_2_gt, comparator_2_eq);
  or or_12 (or_12_out, accA___regC___accB___regD, accA__lt__regC);
  RAMDualAccess #(.AddrBits(8), .Bits(14)) pRAM (
    .str(progLoad), .C(clk), .ld(holdstart), .A1(multiplexer_18_out), .Din1(progIn), .A2(multiplexer_30_out),
    .D1(checkInput), .D2(pRAM_d2));
  Register #(.Bits(8)) A (.D(multiplexer_32_out), .C(clk), .en(or_10_out), .Q(out_14));
  Multiplexer #(.Bits(14)) multiplexer_33 (.sel(holdstop), .in_0(pRAM_d2), .in_1({14{1'b0}}), .out({out_17, out_18}));
  Multiplexer #(.Bits(8)) multiplexer_34 (
    .sel(accB__lt__Operand), .in_0({8{1'b0}}), .in_1(out_18), .out(B__lt__operand));
  Multiplexer #(.Bits(8)) multiplexer_35 (.sel(accB__lt__accA), .in_0({8{1'b0}}), .in_1(out_14), .out(B__lt__A));
  Multiplexer #(.Bits(8)) multiplexer_36 (
    .sel(accA___regC___accB___regD), .in_0({8{1'b0}}), .in_1(out_21), .out(B__lt__D));
  Multiplexer #(.Bits(8)) multiplexer_37 (.sel(reset), .in_0(Binput), .in_1({8{1'b0}}), .out(multiplexer_37_out));
  or or_13 (or_13_out, SelB, reset);
  assign Ainput = A__lt__operand | A__lt__B | A__lt__C | A__lt__D | A__lt__pRAM | A__lt__rRAM | A_plus_B | A_B_t_t | A_B_t | A_B_t_t_t | A_B | A_B_t_t_t_t | A_t | A_and_B | A_or_B | A_xor_B | A__gt__gt__gt__B | A__gt__gt__B | A__lt__lt__lt__B | A__lt__lt__B;  // Or or_14, 8 bits wide
  Register #(.Bits(8)) B (.D(multiplexer_37_out), .C(clk), .en(or_13_out), .Q(out_15));
  assign input_D = D__lt__N | D__lt__M | D__lt__A;  // Or or_15, 8 bits wide
  Decoder #(.Selector_Bits(6)) decoder_3 (
    .sel(out_17), .out_0(Nope), .out_1(accA__lt__Operand), .out_2(accB__lt__Operand), .out_3(accA__lt__accB),
    .out_4(accB__lt__accA), .out_5(regC__lt__accA), .out_6(accA__lt__regC), .out_7(regD__lt__accA),
    .out_8(accA__lt__regD), .out_9(regC__lt__M), .out_10(regC__lt__N), .out_11(regD__lt__M),
    .out_12(regD__lt__N), .out_13(regC___M___regD___N), .out_14(accA___regC___accB___regD),
    .out_15(accA___pRAM_adr_Operand), .out_16(accA___rRAM_adr_Operand), .out_17(rRAM_adr_Operand____accA),
    .out_18(Jump_to_address_Operand), .out_19(Jump_to_address_Operand_if_eq),
    .out_20(Jump_to_address_Operand_if_gr), .out_21(Jump_to_address_Operand_if_le),
    .out_22(Jump_to_address_Operand_if_eq_or_gr), .out_23(Jump_to_address_Operand_if_eq_or_le),
    .out_32(accA___accA__plus__accB), .out_33(accA___accA___accB_t_t), .out_34(accA___accA___accB_t),
    .out_35(accA___accA___accB_t_t_t), .out_36(accA___accA___accB), .out_37(accA___accA___accB_t_t_t_t),
    .out_40(accA___NOT_accA), .out_41(accA___accA_AND_accB), .out_42(accA___accA_OR_accB),
    .out_43(accA___accA_XOR_accB), .out_44(accA___accA__lt__lt__accB),
    .out_45(accA___accA__lt__lt__lt__accB), .out_46(accA___accA__gt__gt__accB),
    .out_47(accA___accA__gt__gt__gt__accB), .out_48(accA_CMP_accB), .out_49(isPrime_accA),
    .out_50(accB___accA), .out_51(rRAM_0x0E_0x0F____LCM__rRAM_adr_Operand__7_4______rRAM_adr_Operand__3_0),
    .out_52(Future_1), .out_53(Future_2), .out_63(STOP));  // open: out_24, out_25, out_26, out_27, out_28, out_29, out_30, out_31, out_38, out_39, out_54, out_55, out_56, out_57, out_58, out_59, out_60, out_61, out_62
  assign Binput = B__lt__operand | B__lt__A | B__lt__D;  // Or or_16, 8 bits wide
  assign input_C = C__lt__N | C__lt__M | C__lt__A;  // Or or_17, 8 bits wide
  Multiplexer #(.Bits(8)) multiplexer_38 (.sel(reset), .in_0(input_C), .in_1({8{1'b0}}), .out(multiplexer_38_out));
  Multiplexer #(.Bits(8)) multiplexer_39 (.sel(regC__lt__accA), .in_0({8{1'b0}}), .in_1(out_14), .out(C__lt__A));
  Multiplexer #(.Bits(8)) multiplexer_40 (.sel(or_19_out), .in_0({8{1'b0}}), .in_1(M_t), .out(C__lt__M));
  Multiplexer #(.Bits(8)) multiplexer_41 (.sel(regC__lt__N), .in_0({8{1'b0}}), .in_1(N_t), .out(C__lt__N));
  or or_18 (or_18_out, SelC, reset);
  Register #(.Bits(8)) C (.D(multiplexer_38_out), .C(clk), .en(or_18_out), .Q(out_20));
  or or_19 (or_19_out, regC___M___regD___N, regC__lt__M);
  Multiplexer #(.Bits(8)) multiplexer_42 (.sel(reset), .in_0(input_D), .in_1({8{1'b0}}), .out(multiplexer_42_out));
  or or_20 (or_20_out, SelD, reset);
  Multiplexer #(.Bits(8)) multiplexer_43 (.sel(regD__lt__accA), .in_0({8{1'b0}}), .in_1(out_14), .out(D__lt__A));
  Multiplexer #(.Bits(8)) multiplexer_44 (.sel(regD__lt__M), .in_0({8{1'b0}}), .in_1(M_t), .out(D__lt__M));
  Multiplexer #(.Bits(8)) multiplexer_45 (.sel(or_25_out), .in_0({8{1'b0}}), .in_1(N_t), .out(D__lt__N));
  or or_21 (SelA, accA__lt__Operand, accA__lt__accB, accA__lt__regC, accA__lt__regD, accA___regC___accB___regD, accA___pRAM_adr_Operand, accA___rRAM_adr_Operand, accA___accA__plus__accB, accA___accA___accB_t_t, accA___accA___accB_t, accA___accA___accB_t_t_t, accA___accA___accB, accA___accA___accB_t_t_t_t, accA___NOT_accA, accA___accA_AND_accB, accA___accA_OR_accB, accA___accA_XOR_accB, accA___accA__lt__lt__accB, accA___accA__lt__lt__lt__accB, accA___accA__gt__gt__accB, accA___accA__gt__gt__gt__accB);
  or or_22 (SelB, accB__lt__Operand, accB__lt__accA, accA___regC___accB___regD);
  or or_23 (SelC, regC__lt__accA, regC__lt__M, regC__lt__N, regC___M___regD___N);
  or or_24 (SelD, regD__lt__accA, regD__lt__M, regD__lt__N, regC___M___regD___N);
  Register #(.Bits(8)) D (.D(multiplexer_42_out), .C(clk), .en(or_20_out), .Q(out_21));
  or or_25 (or_25_out, regC___M___regD___N, regD__lt__N);
  Add #(.Bits(8)) u_A_plus_B (.a(out_14), .b(out_15), .c_i(1'b0), .s(A_plus_B_s));  // open: c_o
  Sub #(.Bits(8)) u_A_B (.a(out_14), .b(out_15), .c_i(1'b0), .s(A_B_s));  // open: c_o
  Div #(.Bits(8)) A_B___A_B (.a(out_14), .b(out_15), .q(A_B___A_B_q), .r(A___B));
  assign not_4_out = ~out_14;  // Not not_4, 8 bits wide
  assign and_3_out = out_14 & out_15;  // And and_3, 8 bits wide
  assign or_26_out = out_14 | out_15;  // Or or_26, 8 bits wide
  assign xor_1_out = out_14 ^ out_15;  // XOr xor_1, 8 bits wide
  Mul #(.Bits(4)) A_B_2 (.a(out_14[3:0]), .b(out_15[3:0]), .mul(A_B_2_mul));
  Comparator #(.Signed("true"), .Bits(8)) Compare (.a(out_14), .b(out_15), .gt(gt), .eq(Compare_eq), .lt(lt));
  ROM #(.AddrBits(8)) prime (.A(out_14), .sel(1'b1), .D(prime_d));
  Comparator #(.Bits(8)) Compare_2 (.a(A___B), .b({8{1'b0}}), .eq(Compare_2_eq));  // open: gt, lt
  Multiplexer #(.Bits(8)) multiplexer_46 (
    .sel(accA___accA__plus__accB), .in_0({8{1'b0}}), .in_1(A_plus_B_s), .out(A_plus_B));
  Multiplexer #(.Bits(8)) multiplexer_47 (.sel(accA___accA___accB_t_t), .in_0({8{1'b0}}), .in_1(A_B_s), .out(A_B_t_t));
  Multiplexer #(.Bits(8)) multiplexer_48 (.sel(accA___accA___accB_t), .in_0({8{1'b0}}), .in_1(A_B_2_mul), .out(A_B_t));
  Multiplexer #(.Bits(8)) multiplexer_49 (
    .sel(accA___accA___accB_t_t_t), .in_0({8{1'b0}}), .in_1(A_B___A_B_q), .out(A_B_t_t_t));
  Multiplexer #(.Bits(8)) multiplexer_50 (.sel(accA___accA___accB), .in_0({8{1'b0}}), .in_1(A___B), .out(A_B));
  Multiplexer #(.Bits(8)) multiplexer_51 (.sel(accA___NOT_accA), .in_0({8{1'b0}}), .in_1(not_4_out), .out(A_t));
  Multiplexer #(.Bits(8)) multiplexer_52 (
    .sel(accA___accA_AND_accB), .in_0({8{1'b0}}), .in_1(and_3_out), .out(A_and_B));
  Multiplexer #(.Bits(8)) multiplexer_53 (.sel(accA___accA_OR_accB), .in_0({8{1'b0}}), .in_1(or_26_out), .out(A_or_B));
  Multiplexer #(.Bits(8)) multiplexer_54 (
    .sel(accA___accA_XOR_accB), .in_0({8{1'b0}}), .in_1(xor_1_out), .out(A_xor_B));
  Multiplexer #(.Selector_Bits(2)) multiplexer_55 (
    .sel(out_17[1:0]), .in_0(Compare_eq), .in_1(prime_d), .in_2(Compare_2_eq), .in_3(notconnected_14_out),
    .out(eq));
  // NotConnected on notconnected_14_out
  Mul #(.Bits(8)) mul_2 (.a(out_14), .b(out_14), .mul(mul_2_mul));
  Mul #(.Bits(8)) mul_3 (.a(mul_2_mul[7:0]), .b(out_14), .mul(mul_3_mul));
  Mul #(.Bits(8)) mul_4 (.a(mul_3_mul[7:0]), .b(out_14), .mul(mul_4_mul));
  BarrelShifter #(.Bits(8)) barrelshifter_1 (.in(out_14), .shift({1'b0, out_15[2:0]}), .out(barrelshifter_1_out));
  BarrelShifter #(.Bits(8), .barrelShifterMode("rotate")) barrelshifter_2 (
    .in(out_14), .shift({1'b0, out_15[2:0]}), .out(barrelshifter_2_out));
  BarrelShifter #(.Bits(8), .direction("right")) barrelshifter_3 (
    .in(out_14), .shift({1'b0, out_15[2:0]}), .out(barrelshifter_3_out));
  BarrelShifter #(.Bits(8), .barrelShifterMode("rotate"), .direction("right")) barrelshifter_4 (
    .in(out_14), .shift({1'b0, out_15[2:0]}), .out(barrelshifter_4_out));
  ROM #(.AddrBits(16), .Bits(16)) LCM (.A({out_22, out_23}), .sel(1'b1), .D(out_30));
  Mul #(.Bits(8)) mul_5 (.a(mul_4_mul[7:0]), .b(out_14), .mul(mul_5_mul));
  Multiplexer #(.Bits(8)) multiplexer_56 (
    .sel(accA___accA__lt__lt__accB), .in_0({8{1'b0}}), .in_1(barrelshifter_1_out), .out(A__lt__lt__B));
  Multiplexer #(.Bits(8)) multiplexer_57 (
    .sel(accA___accA__lt__lt__lt__accB), .in_0({8{1'b0}}), .in_1(barrelshifter_2_out), .out(A__lt__lt__lt__B));
  Multiplexer #(.Bits(8)) multiplexer_58 (
    .sel(accA___accA__gt__gt__accB), .in_0({8{1'b0}}), .in_1(barrelshifter_3_out), .out(A__gt__gt__B));
  Multiplexer #(.Bits(8)) multiplexer_59 (
    .sel(accA___accA__gt__gt__gt__accB), .in_0({8{1'b0}}), .in_1(barrelshifter_4_out), .out(A__gt__gt__gt__B));
  Mul #(.Bits(8)) mul_6 (.a(mul_5_mul[7:0]), .b(out_14), .mul(mul_6_mul));
  Register #(.Bits(16)) register_3 (.D(out_30), .C(clk), .en(S0_lcm), .Q({out_25, out_24}));
  Mul #(.Bits(8)) mul_7 (.a(mul_6_mul[7:0]), .b(out_14), .mul(mul_7_mul));
  Multiplexer #(.Selector_Bits(3), .Bits(8)) multiplexer_60 (
    .sel(out_15[2:0]), .in_0(8'h1), .in_1(out_14), .in_2(mul_2_mul[7:0]), .in_3(mul_3_mul[7:0]),
    .in_4(mul_4_mul[7:0]), .in_5(mul_5_mul[7:0]), .in_6(mul_6_mul[7:0]), .in_7(mul_7_mul[7:0]),
    .out(multiplexer_60_out));
  Multiplexer #(.Bits(8)) multiplexer_61 (
    .sel(accA___accA___accB_t_t_t_t), .in_0({8{1'b0}}), .in_1(multiplexer_60_out), .out(A_B_t_t_t_t));
  or or_27 (or_27_out, equal, greater);
  or or_28 (or_28_out, equal, lesser);
  and and_4 (and_4_out, Jump_to_address_Operand_if_eq, equal);
  and and_5 (and_5_out, Jump_to_address_Operand_if_gr, greater);
  and and_6 (and_6_out, Jump_to_address_Operand_if_le, lesser);
  and and_7 (and_7_out, Jump_to_address_Operand_if_eq_or_gr, or_27_out);
  and and_8 (and_8_out, Jump_to_address_Operand_if_eq_or_le, or_28_out);
  or or_29 (jump, Jump_to_address_Operand, and_4_out, and_5_out, and_6_out, and_7_out, and_8_out);
  Register u_equal (.D(eq), .C(clk), .en(eneq), .Q(equal));
  Register u_greater (.D(gt), .C(clk), .en(accA_CMP_accB), .Q(greater));
  Register less (.D(lt), .C(clk), .en(accA_CMP_accB), .Q(lesser));
  or or_30 (eneq, accB___accA, isPrime_accA, accA_CMP_accB);

  assign out_16 = checkInput[7:0];
  assign out_19 = out_17;
  assign out_26 = out_23;
  assign out_27 = out_22;
  assign \output  = out_23;

  // Other names for the same wires on the sheet: operand[7:0] = out_18; opcode[5:0] = out_17; _0F[7:0] = out_24;
  //   _0E[7:0] = out_25; A[7:0] = out_14; B[7:0] = out_15; LSB_B_Fact[7:0] = B_Fact[7:0];
  //   MSB_B_Fact[7:0] = B_Fact[15:8]; C[7:0] = out_20; _8_bits_right[7:0] = checkInput[7:0]; D[7:0] = out_21;
  //   Rout2[7:0] = out_23; Rout1[7:0] = out_22; rRAM_check[7:0] = out_22

  // Notes on the sheet:
  //   Group Members
  //   6833140621 Nadeef Salaeh (Main Curcuit Developer)
  //   6833222421 Phumsith Sirichotevanich
  //   6833116621 Torntep Charusombut
  //   6833045721 Chawanwat Lueangsirinapha (Main Circuit Developer)
  //   pRAM
  //   rRAM
  //   Selectors
  //   Load A
  //   Register
  //   Load B
  //   Input A B C D
  //   Decoder Opcode
  //   Load & Jump tunnel
  //   ALU tunnel
  //   Load C
  //   Selector A B C D
  //   Load D
  //   ALU
  //   +-*/%^
  //   Bitswise & Shift
  //   Set Compare Flags
  //   contents of prime (hex, n*v repeats v):
  //   0,0,1,1,0,1,0,1,0,0,0,1,0,1,0,0,0,1,0,1,0,0,0,1,5*0,1,0,1,5*0
  //   ,1,0,0,0,1,0,1,0,0,0,1,5*0,1,5*0,1,0,1,5*0,1,0,0,0,1,0,1,5*0,1
  //   ,0,0,0,1,5*0,1,7*0,1,0,0,0,1,0,1,0,0,0,1,0,1,0,0,0,1,13*0,1,0,0,0
  //   ,1,5*0,1,0,1,9*0,1,0,1,5*0,1,5*0,1,0,0,0,1,5*0,1,5*0,1,0,1,9*0
  //   ,1,0,1,0,0,0,1,0,1,11*0,1,11*0,1,0,0,0,1,0,1,0,0,0,1,5*0,1,0,1
  //   ,9*0,1
  //   contents of LCM (hex, n*v repeats v):
  //   257*0,1,2,3,4,5,6,7,8,9,a,b,c,d,e,f,10,11,12,13,14,15,16,17,18
  //   ,19,1a,1b,1c,1d,1e,1f,20,21,22,23,24,25,26,27,28,29,2a,2b,2c,2d
  //   ,2e,2f,30,31,32,33,34,35,36,37,38,39,3a,3b,3c,3d,3e,3f,40,41,42
  //   ,43,44,45,46,47,48,49,4a,4b,4c,4d,4e,4f,50,51,52,53,54,55,56,57
  //   ,58,59,5a,5b,5c,5d,5e,5f,60,61,62,63,64,65,66,67,68,69,6a,6b,6c
  //   ,6d,6e,6f,70,71,72,73,74,75,76,77,78,79,7a,7b,7c,7d,7e,7f,80,81
  //   ,82,83,84,85,86,87,88,89,8a,8b,8c,8d,8e,8f,90,91,92,93,94,95,96
  //   ,97,98,99,9a,9b,9c,9d,9e,9f,a0,a1,a2,a3,a4,a5,a6,a7,a8,a9,aa,ab
  //   ,ac,ad,ae,af,b0,b1,b2,b3,b4,b5,b6,b7,b8,b9,ba,bb,bc,bd,be,bf,c0
  //   ,c1,c2,c3,c4,c5,c6,c7,c8,c9,ca,cb,cc,cd,ce,cf,d0,d1,d2,d3,d4,d5
  //   ,d6,d7,d8,d9,da,db,dc,dd,de,df,e0,e1,e2,e3,e4,e5,e6,e7,e8,e9,ea
  //   ,eb,ec,ed,ee,ef,f0,f1,f2,f3,f4,f5,f6,f7,f8,f9,fa,fb,fc,fd,fe,ff
  //   ,0,2,2,6,4,a,6,e,8,12,a,16,c,1a,e,1e,10,22,12,26,14,2a,16,2e,18
  //   ,32,1a,36,1c,3a,1e,3e,20,42,22,46,24,4a,26,4e,28,52,2a,56,2c,5a
  //   ,2e,5e,30,62,32,66,34,6a,36,6e,38,72,3a,76,3c,7a,3e,7e,40,82,42
  //   ,86,44,8a,46,8e,48,92,4a,96,4c,9a,4e,9e,50,a2,52,a6,54,aa,56,ae
  //   ,58,b2,5a,b6,5c,ba,5e,be,60,c2,62,c6,64,ca,66,ce,68,d2,6a,d6,6c
  //   ,da,6e,de,70,e2,72,e6,74,ea,76,ee,78,f2,7a,f6,7c,fa,7e,fe,80,102
  //   ,82,106,84,10a,86,10e,88,112,8a,116,8c,11a,8e,11e,90,122,92,126
  //   ,94,12a,96,12e,98,132,9a,136,9c,13a,9e,13e,a0,142,a2,146,a4,14a
  //   ,a6,14e,a8,152,aa,156,ac,15a,ae,15e,b0,162,b2,166,b4,16a,b6,16e
  //   ,b8,172,ba,176,bc,17a,be,17e,c0,182,c2,186,c4,18a,c6,18e,c8,192
  //   ,ca,196,cc,19a,ce,19e,d0,1a2,d2,1a6,d4,1aa,d6,1ae,d8,1b2,da,1b6
  //   ,dc,1ba,de,1be,e0,1c2,e2,1c6,e4,1ca,e6,1ce,e8,1d2,ea,1d6,ec,1da
  //   ,ee,1de,f0,1e2,f2,1e6,f4,1ea,f6,1ee,f8,1f2,fa,1f6,fc,1fa,fe,1fe
  //   ,0,3,6,3,c,f,6,15,18,9,1e,21,c,27,2a,f,30,33,12,39,3c,15,42,45
  //   ,18,4b,4e,1b,54,57,1e,5d,60,21,66,69,24,6f,72,27,78,7b,2a,81,84
  //   ,2d,8a,8d,30,93,96,33,9c,9f,36,a5,a8,39,ae,b1,3c,b7,ba,3f,c0,c3
  //   ,42,c9,cc,45,d2,d5,48,db,de,4b,e4,e7,4e,ed,f0,51,f6,f9,54,ff,102
  //   ,57,108,10b,5a,111,114,5d,11a,11d,60,123,126,63,12c,12f,66,135
  //   ,138,69,13e,141,6c,147,14a,6f,150,153,72,159,15c,75,162,165,78
  //   ,16b,16e,7b,174,177,7e,17d,180,81,186,189,84,18f,192,87,198,19b
  //   ,8a,1a1,1a4,8d,1aa,1ad,90,1b3,1b6,93,1bc,1bf,96,1c5,1c8,99,1ce
  //   ,1d1,9c,1d7,1da,9f,1e0,1e3,a2,1e9,1ec,a5,1f2,1f5,a8,1fb,1fe,ab
  //   ,204,207,ae,20d,210,b1,216,219,b4,21f,222,b7,228,22b,ba,231,234
  //   ,bd,23a,23d,c0,243,246,c3,24c,24f,c6,255,258,c9,25e,261,cc,267
  //   ,26a,cf,270,273,d2,279,27c,d5,282,285,d8,28b,28e,db,294,297,de
  //   ,29d,2a0,e1,2a6,2a9,e4,2af,2b2,e7,2b8,2bb,ea,2c1,2c4,ed,2ca,2cd
  //   ,f0,2d3,2d6,f3,2dc,2df,f6,2e5,2e8,f9,2ee,2f1,fc,2f7,2fa,ff,0,4,4
  //   ,c,4,14,c,1c,8,24,14,2c,c,34,1c,3c,10,44,24,4c,14,54,2c,5c,18
  //   ,64,34,6c,1c,74,3c,7c,20,84,44,8c,24,94,4c,9c,28,a4,54,ac,2c,b4
  //   ,5c,bc,30,c4,64,cc,34,d4,6c,dc,38,e4,74,ec,3c,f4,7c,fc,40,104
  //   ,84,10c,44,114,8c,11c,48,124,94,12c,4c,134,9c,13c,50,144,a4,14c
  //   ,54,154,ac,15c,58,164,b4,16c,5c,174,bc,17c,60,184,c4,18c,64,194
  //   ,cc,19c,68,1a4,d4,1ac,6c,1b4,dc,1bc,70,1c4,e4,1cc,74,1d4,ec,1dc
  //   ,78,1e4,f4,1ec,7c,1f4,fc,1fc,80,204,104,20c,84,214,10c,21c,88
  //   ,224,114,22c,8c,234,11c,23c,90,244,124,24c,94,254,12c,25c,98,264
  //   ,134,26c,9c,274,13c,27c,a0,284,144,28c,a4,294,14c,29c,a8,2a4,154
  //   ,2ac,ac,2b4,15c,2bc,b0,2c4,164,2cc,b4,2d4,16c,2dc,b8,2e4,174,2ec
  //   ,bc,2f4,17c,2fc,c0,304,184,30c,c4,314,18c,31c,c8,324,194,32c,cc
  //   ,334,19c,33c,d0,344,1a4,34c,d4,354,1ac,35c,d8,364,1b4,36c,dc,374
  //   ,1bc,37c,e0,384,1c4,38c,e4,394,1cc,39c,e8,3a4,1d4,3ac,ec,3b4,1dc
  //   ,3bc,f0,3c4,1e4,3cc,f4,3d4,1ec,3dc,f8,3e4,1f4,3ec,fc,3f4,1fc,3fc
  //   ,0,5,a,f,14,5,1e,23,28,2d,a,37,3c,41,46,f,50,55,5a,5f,14,69,6e
  //   ,73,78,19,82,87,8c,91,1e,9b,a0,a5,aa,23,b4,b9,be,c3,28,cd,d2,d7
  //   ,dc,2d,e6,eb,f0,f5,32,ff,104,109,10e,37,118,11d,122,127,3c,131
  //   ,136,13b,140,41,14a,14f,154,159,46,163,168,16d,172,4b,17c,181
  //   ,186,18b,50,195,19a,19f,1a4,55,1ae,1b3,1b8,1bd,5a,1c7,1cc,1d1
  //   ,1d6,5f,1e0,1e5,1ea,1ef,64,1f9,1fe,203,208,69,212,217,21c,221
  //   ,6e,22b,230,235,23a,73,244,249,24e,253,78,25d,262,267,26c,7d,276
  //   ,27b,280,285,82,28f,294,299,29e,87,2a8,2ad,2b2,2b7,8c,2c1,2c6
  //   ,2cb,2d0,91,2da,2df,2e4,2e9,96,2f3,2f8,2fd,302,9b,30c,311,316
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  //   Jump
  //   Compare Flag
endmodule

/* Test case 01_P01T2:
M N progIn reset progLoad start result clk valid done output
0 0      0     0        0     0      0   0     x    x      x
0 0      0     0        0     0      0   1     x    x      x
0 0      0     1        0     0      0   0     x    x      x
0 0      0     1        0     0      0   1     0    0      x
0 0      0     0        0     0      0   0     0    0      x
0 0      0     0        0     0      0   1     0    0      x
0 0      0     0        0     0      0   0     0    0      x
0 0      0     0        0     0      0   1     0    0      x
0 0      0     0        0     0      0   0     0    0      x
0 0      0     0        0     0      0   1     0    0      x
0 0      0     0        0     0      0   0     0    0      x
0 0      0     0        0     0      0   1     0    0      x
0 0      0     0        0     0      0   0     0    0      x
0 0      0     0        0     0      0   1     0    0      x
0 0      0     0        0     0      0   0     0    0      x
0 0      0     0        0     0      0   1     0    0      x
0 0      0     0        0     0      0   0     0    0      x
0 0      0     0        0     0      0   1     0    0      x
0 0      0     0        0     0      0   0     0    0      x
0 0      0     0        0     0      0   1     0    0      x
0 0      0     0        0     0      0   0     0    0      x
0 0      0     0        0     0      0   1     0    0      x
0 0      0     0        0     0      0   0     0    0      x
0 0      0     0        0     0      0   1     0    0      x
0 0      0     0        0     0      0   0     0    0      x
0 0      0     0        0     0      0   1     0    0      x
0 0      0     0        0     0      0   0     0    0      x
0 0      0     0        0     0      0   1     0    0      x
0 0      0     0        0     0      0   0     0    0      x
0 0      0     0        0     0      0   1     0    0      x
0 0      0     0        0     0      0   0     0    0      x
0 0      0     0        0     0      0   1     0    0      x
0 0      0     0        0     0      0   0     0    0      x
0 0      0     0        0     0      0   1     0    0      x
0 0      0     0        0     0      0   0     0    0      x
0 0      0     0        0     0      0   1     0    0      x
0 0      0     0        0     0      0   0     0    0      x
0 0      0     0        0     0      0   1     0    0      x
0 0      0     0        0     0      0   0     0    0      x
0 0      0     0        0     0      0   1     0    0      x
0 0      0     0        0     0      0   0     0    0      x
0 0      0     0        0     0      0   1     0    0      x
0 0    271     0        1     0      0   0     0    0      x
0 0    271     0        1     0      0   1     0    0      x
0 0    565     0        1     0      0   0     0    0      x
0 0    565     0        1     0      0   1     0    0      x
0 0   8192     0        1     0      0   0     0    0      x
0 0   8192     0        1     0      0   1     0    0      x
0 0   4355     0        1     0      0   0     0    0      x
0 0   4355     0        1     0      0   1     0    0      x
0 0  16128     0        1     0      0   0     0    0      x
0 0  16128     0        1     0      0   1     0    0      x
0 0      0     0        0     1      0   0     0    0      x
0 0      0     0        0     1      0   1     0    0      x
0 0      0     0        0     0      0   0     x    0      x
0 0      0     0        0     0      0   1     x    0      x
0 0      0     0        0     0      0   0     x    0      x
0 0      0     0        0     0      0   1     x    0      x
0 0      0     0        0     0      0   0     x    0      x
0 0      0     0        0     0      0   1     x    0      x
0 0      0     0        0     0      0   0     x    0      x
0 0      0     0        0     0      0   1     x    0      x
0 0      0     0        0     0      0   0     x    0      x
0 0      0     0        0     0      0   1     x    0      x
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*/

/* Test case 06_P04T2:
M N progIn reset progLoad start result clk valid done output
0 0      0     0        0     0      0   0     x    x      x
0 0      0     0        0     0      0   1     x    x      x
0 0      0     1        0     0      0   0     x    x      x
0 0      0     1        0     0      0   1     0    0      x
0 0      0     0        0     0      0   0     0    0      x
0 0      0     0        0     0      0   1     0    0      x
0 0      0     0        0     0      0   0     0    0      x
0 0      0     0        0     0      0   1     0    0      x
0 0      0     0        0     0      0   0     0    0      x
0 0      0     0        0     0      0   1     0    0      x
0 0      0     0        0     0      0   0     0    0      x
0 0      0     0        0     0      0   1     0    0      x
0 0      0     0        0     0      0   0     0    0      x
0 0      0     0        0     0      0   1     0    0      x
0 0      0     0        0     0      0   0     0    0      x
0 0      0     0        0     0      0   1     0    0      x
0 0      0     0        0     0      0   0     0    0      x
0 0      0     0        0     0      0   1     0    0      x
0 0      0     0        0     0      0   0     0    0      x
0 0      0     0        0     0      0   1     0    0      x
0 0      0     0        0     0      0   0     0    0      x
0 0      0     0        0     0      0   1     0    0      x
0 0      0     0        0     0      0   0     0    0      x
0 0      0     0        0     0      0   1     0    0      x
0 0      0     0        0     0      0   0     0    0      x
0 0      0     0        0     0      0   1     0    0      x
0 0      0     0        0     0      0   0     0    0      x
0 0      0     0        0     0      0   1     0    0      x
0 0      0     0        0     0      0   0     0    0      x
0 0      0     0        0     0      0   1     0    0      x
0 0      0     0        0     0      0   0     0    0      x
0 0      0     0        0     0      0   1     0    0      x
0 0      0     0        0     0      0   0     0    0      x
0 0      0     0        0     0      0   1     0    0      x
0 0      0     0        0     0      0   0     0    0      x
0 0      0     0        0     0      0   1     0    0      x
0 0      0     0        0     0      0   0     0    0      x
0 0      0     0        0     0      0   1     0    0      x
0 0      0     0        0     0      0   0     0    0      x
0 0      0     0        0     0      0   1     0    0      x
0 0      0     0        0     0      0   0     0    0      x
0 0      0     0        0     0      0   1     0    0      x
0 0      0     0        0     0      0   0     0    0      x
0 0      0     0        0     0      0   1     0    0      x
0 0    271     0        1     0      0   0     0    0      x
0 0    271     0        1     0      0   1     0    0      x
0 0  12544     0        1     0      0   0     0    0      x
0 0  12544     0        1     0      0   1     0    0      x
0 0   4864     0        1     0      0   0     0    0      x
0 0   4864     0        1     0      0   1     0    0      x
0 0    257     0        1     0      0   0     0    0      x
0 0    257     0        1     0      0   1     0    0      x
0 0   4867     0        1     0      0   0     0    0      x
0 0   4867     0        1     0      0   1     0    0      x
0 0    455     0        1     0      0   0     0    0      x
0 0    455     0        1     0      0   1     0    0      x
0 0  12544     0        1     0      0   0     0    0      x
0 0  12544     0        1     0      0   1     0    0      x
0 0   4873     0        1     0      0   0     0    0      x
0 0   4873     0        1     0      0   1     0    0      x
0 0   4354     0        1     0      0   0     0    0      x
0 0   4354     0        1     0      0   1     0    0      x
0 0   4355     0        1     0      0   0     0    0      x
0 0   4355     0        1     0      0   1     0    0      x
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*/

/* Test case 11_P07T3:
M N progIn reset progLoad start result clk valid done output
0 0      0     0        0     0      0   0     x    x      x
0 0      0     0        0     0      0   1     x    x      x
0 0      0     1        0     0      0   0     x    x      x
0 0      0     1        0     0      0   1     0    0      x
0 0      0     0        0     0      0   0     0    0      x
0 0      0     0        0     0      0   1     0    0      x
0 0      0     0        0     0      0   0     0    0      x
0 0      0     0        0     0      0   1     0    0      x
0 0      0     0        0     0      0   0     0    0      x
0 0      0     0        0     0      0   1     0    0      x
0 0      0     0        0     0      0   0     0    0      x
0 0      0     0        0     0      0   1     0    0      x
0 0      0     0        0     0      0   0     0    0      x
0 0      0     0        0     0      0   1     0    0      x
0 0      0     0        0     0      0   0     0    0      x
0 0      0     0        0     0      0   1     0    0      x
0 0      0     0        0     0      0   0     0    0      x
0 0      0     0        0     0      0   1     0    0      x
0 0      0     0        0     0      0   0     0    0      x
0 0      0     0        0     0      0   1     0    0      x
0 0      0     0        0     0      0   0     0    0      x
0 0      0     0        0     0      0   1     0    0      x
0 0      0     0        0     0      0   0     0    0      x
0 0      0     0        0     0      0   1     0    0      x
0 0      0     0        0     0      0   0     0    0      x
0 0      0     0        0     0      0   1     0    0      x
0 0      0     0        0     0      0   0     0    0      x
0 0      0     0        0     0      0   1     0    0      x
0 0      0     0        0     0      0   0     0    0      x
0 0      0     0        0     0      0   1     0    0      x
0 0      0     0        0     0      0   0     0    0      x
0 0      0     0        0     0      0   1     0    0      x
0 0      0     0        0     0      0   0     0    0      x
0 0      0     0        0     0      0   1     0    0      x
0 0      0     0        0     0      0   0     0    0      x
0 0      0     0        0     0      0   1     0    0      x
0 0      0     0        0     0      0   0     0    0      x
0 0      0     0        0     0      0   1     0    0      x
0 0      0     0        0     0      0   0     0    0      x
0 0      0     0        0     0      0   1     0    0      x
0 0      0     0        0     0      0   0     0    0      x
0 0      0     0        0     0      0   1     0    0      x
0 0      0     0        0     0      0   0     0    0      x
0 0      0     0        0     0      0   1     0    0      x
0 0    446     0        1     0      0   0     0    0      x
0 0    446     0        1     0      0   1     0    0      x
0 0   4353     0        1     0      0   0     0    0      x
0 0   4353     0        1     0      0   1     0    0      x
0 0    426     0        1     0      0   0     0    0      x
0 0    426     0        1     0      0   1     0    0      x
0 0   4367     0        1     0      0   0     0    0      x
0 0   4367     0        1     0      0   1     0    0      x
0 0  13087     0        1     0      0   0     0    0      x
0 0  13087     0        1     0      0   1     0    0      x
0 0  16128     0        1     0      0   0     0    0      x
0 0  16128     0        1     0      0   1     0    0      x
0 0      0     0        0     0      0   0     0    0      x
0 0      0     0        0     0      0   1     0    0      x
0 0      0     0        0     1      0   0     0    0      x
0 0      0     0        0     1      0   1     0    0      x
0 0      0     0        0     0      0   0     x    0      x
0 0      0     0        0     0      0   1     x    0      x
0 0      0     0        0     0      0   0     x    0      x
0 0      0     0        0     0      0   1     x    0      x
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*/

/* Test case 02_P01T3:
M N progIn reset progLoad start result clk valid done output
0 0      0     0        0     0      0   0     x    x      x
0 0      0     0        0     0      0   1     x    x      x
0 0      0     1        0     0      0   0     x    x      x
0 0      0     1        0     0      0   1     0    0      x
0 0      0     0        0     0      0   0     0    0      x
0 0      0     0        0     0      0   1     0    0      x
0 0      0     0        0     0      0   0     0    0      x
0 0      0     0        0     0      0   1     0    0      x
0 0      0     0        0     0      0   0     0    0      x
0 0      0     0        0     0      0   1     0    0      x
0 0      0     0        0     0      0   0     0    0      x
0 0      0     0        0     0      0   1     0    0      x
0 0      0     0        0     0      0   0     0    0      x
0 0      0     0        0     0      0   1     0    0      x
0 0      0     0        0     0      0   0     0    0      x
0 0      0     0        0     0      0   1     0    0      x
0 0      0     0        0     0      0   0     0    0      x
0 0      0     0        0     0      0   1     0    0      x
0 0      0     0        0     0      0   0     0    0      x
0 0      0     0        0     0      0   1     0    0      x
0 0      0     0        0     0      0   0     0    0      x
0 0      0     0        0     0      0   1     0    0      x
0 0      0     0        0     0      0   0     0    0      x
0 0      0     0        0     0      0   1     0    0      x
0 0      0     0        0     0      0   0     0    0      x
0 0      0     0        0     0      0   1     0    0      x
0 0      0     0        0     0      0   0     0    0      x
0 0      0     0        0     0      0   1     0    0      x
0 0      0     0        0     0      0   0     0    0      x
0 0      0     0        0     0      0   1     0    0      x
0 0      0     0        0     0      0   0     0    0      x
0 0      0     0        0     0      0   1     0    0      x
0 0      0     0        0     0      0   0     0    0      x
0 0      0     0        0     0      0   1     0    0      x
0 0      0     0        0     0      0   0     0    0      x
0 0      0     0        0     0      0   1     0    0      x
0 0      0     0        0     0      0   0     0    0      x
0 0      0     0        0     0      0   1     0    0      x
0 0      0     0        0     0      0   0     0    0      x
0 0      0     0        0     0      0   1     0    0      x
0 0      0     0        0     0      0   0     0    0      x
0 0      0     0        0     0      0   1     0    0      x
0 0    271     0        1     0      0   0     0    0      x
0 0    271     0        1     0      0   1     0    0      x
0 0    565     0        1     0      0   0     0    0      x
0 0    565     0        1     0      0   1     0    0      x
0 0   8192     0        1     0      0   0     0    0      x
0 0   8192     0        1     0      0   1     0    0      x
0 0   4355     0        1     0      0   0     0    0      x
0 0   4355     0        1     0      0   1     0    0      x
0 0  16128     0        1     0      0   0     0    0      x
0 0  16128     0        1     0      0   1     0    0      x
0 0      0     0        0     1      0   0     0    0      x
0 0      0     0        0     1      0   1     0    0      x
0 0      0     0        0     0      0   0     x    0      x
0 0      0     0        0     0      0   1     x    0      x
0 0      0     0        0     0      0   0     x    0      x
0 0      0     0        0     0      0   1     x    0      x
0 0      0     0        0     0      0   0     x    0      x
0 0      0     0        0     0      0   1     x    0      x
0 0      0     0        0     0      0   0     x    0      x
0 0      0     0        0     0      0   1     x    0      x
0 0      0     0        0     0      0   0     x    0      x
0 0      0     0        0     0      0   1     x    0      x
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*/

/* Test case 07_P05T2:
M N progIn reset progLoad start result clk valid done output
0 0      0     0        0     0      0   0     x    x      x
0 0      0     0        0     0      0   1     x    x      x
0 0      0     1        0     0      0   0     x    x      x
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*/

/* Test case 12_P08T2:
M N progIn reset progLoad start result clk valid done output
0 0      0     0        0     0      0   0     x    x      x
0 0      0     0        0     0      0   1     x    x      x
0 0      0     1        0     0      0   0     x    x      x
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*/

/* Test case 03_P02T2:
M N progIn reset progLoad start result clk valid done output
0 0      0     0        0     0      0   0     x    x      x
0 0      0     0        0     0      0   1     x    x      x
0 0      0     1        0     0      0   0     x    x      x
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*/

/* Test case 08_P06T2:
M N progIn reset progLoad start result clk valid done output
0 0      0     0        0     0      0   0     x    x      x
0 0      0     0        0     0      0   1     x    x      x
0 0      0     1        0     0      0   0     x    x      x
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*/

/* Test case 13_P08T3:
M N progIn reset progLoad start result clk valid done output
0 0      0     0        0     0      0   0     x    x      x
0 0      0     0        0     0      0   1     x    x      x
0 0      0     1        0     0      0   0     x    x      x
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*/

/* Test case 04_P03T2:
M N progIn reset progLoad start result clk valid done output
0 0      0     0        0     0      0   0     x    x      x
0 0      0     0        0     0      0   1     x    x      x
0 0      0     1        0     0      0   0     x    x      x
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*/

/* Test case 09_P06T3:
M N progIn reset progLoad start result clk valid done output
0 0      0     0        0     0      0   0     x    x      x
0 0      0     0        0     0      0   1     x    x      x
0 0      0     1        0     0      0   0     x    x      x
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*/

/* Test case 14_P09T2:
M N progIn reset progLoad start result clk valid done output
0 0      0     0        0     0      0   0     x    x      x
0 0      0     0        0     0      0   1     x    x      x
0 0      0     1        0     0      0   0     x    x      x
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*/

/* Test case 05_P03T3:
M N progIn reset progLoad start result clk valid done output
0 0      0     0        0     0      0   0     x    x      x
0 0      0     0        0     0      0   1     x    x      x
0 0      0     1        0     0      0   0     x    x      x
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*/

/* Test case 10_P07T2:
M N progIn reset progLoad start result clk valid done output
0 0      0     0        0     0      0   0     x    x      x
0 0      0     0        0     0      0   1     x    x      x
0 0      0     1        0     0      0   0     x    x      x
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*/

/* Test case 15_P09T3:
M N progIn reset progLoad start result clk valid done output
0 0      0     0        0     0      0   0     x    x      x
0 0      0     0        0     0      0   1     x    x      x
0 0      0     1        0     0      0   0     x    x      x
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*/

/* Test case 16_P01T03:
M N progIn reset progLoad start result clk valid done output
0 0      0     0        0     0      0   0     x    x      x
0 0      0     0        0     0      0   1     x    x      x
0 0      0     1        0     0      0   0     x    x      x
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*/

/* Test case 21_P05T2:
M N progIn reset progLoad start result clk valid done output
0 0      0     0        0     0      0   0     x    x      x
0 0      0     0        0     0      0   1     x    x      x
0 0      0     1        0     0      0   0     x    x      x
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*/

/* Test case 26_P10T01:
M N progIn reset progLoad start result clk valid done output
0 0      0     0        0     0      0   0     x    x      x
0 0      0     0        0     0      0   1     x    x      x
0 0      0     1        0     0      0   0     x    x      x
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*/

/* Test case 17_P02T02:
M N progIn reset progLoad start result clk valid done output
0 0      0     0        0     0      0   0     x    x      x
0 0      0     0        0     0      0   1     x    x      x
0 0      0     1        0     0      0   0     x    x      x
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*/

/* Test case 22_P06T03:
M N progIn reset progLoad start result clk valid done output
0 0      0     0        0     0      0   0     x    x      x
0 0      0     0        0     0      0   1     x    x      x
0 0      0     1        0     0      0   0     x    x      x
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*/

/* Test case 27_P10T02:
M N progIn reset progLoad start result clk valid done output
0 0      0     0        0     0      0   0     x    x      x
0 0      0     0        0     0      0   1     x    x      x
0 0      0     1        0     0      0   0     x    x      x
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*/

/* Test case 18_P03T03:
M N progIn reset progLoad start result clk valid done output
0 0      0     0        0     0      0   0     x    x      x
0 0      0     0        0     0      0   1     x    x      x
0 0      0     1        0     0      0   0     x    x      x
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*/

/* Test case 23_P07T03:
M N progIn reset progLoad start result clk valid done output
0 0      0     0        0     0      0   0     x    x      x
0 0      0     0        0     0      0   1     x    x      x
0 0      0     1        0     0      0   0     x    x      x
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*/

/* Test case 28_P11T01:
M N progIn reset progLoad start result clk valid done output
0 0      0     0        0     0      0   0     x    x      x
0 0      0     0        0     0      0   1     x    x      x
0 0      0     1        0     0      0   0     x    x      x
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*/

/* Test case 19_P04T02:
M N progIn reset progLoad start result clk valid done output
0 0      0     0        0     0      0   0     x    x      x
0 0      0     0        0     0      0   1     x    x      x
0 0      0     1        0     0      0   0     x    x      x
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*/

/* Test case 24_P08T03:
M N progIn reset progLoad start result clk valid done output
0 0      0     0        0     0      0   0     x    x      x
0 0      0     0        0     0      0   1     x    x      x
0 0      0     1        0     0      0   0     x    x      x
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*/

/* Test case 29_P11T02:
M N progIn reset progLoad start result clk valid done output
0 0      0     0        0     0      0   0     x    x      x
0 0      0     0        0     0      0   1     x    x      x
0 0      0     1        0     0      0   0     x    x      x
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*/

/* Test case 20_P04T03:
M N progIn reset progLoad start result clk valid done output
0 0      0     0        0     0      0   0     x    x      x
0 0      0     0        0     0      0   1     x    x      x
0 0      0     1        0     0      0   0     x    x      x
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*/

/* Test case 25_P09T03:
M N progIn reset progLoad start result clk valid done output
0 0      0     0        0     0      0   0     x    x      x
0 0      0     0        0     0      0   1     x    x      x
0 0      0     1        0     0      0   0     x    x      x
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*/
